# Fritzing sketch boardLayoutAndSchematic (saved by Fritzing 0.9.3b)

parts:
  R0L1 = LEDs [package=led10mm]
  R0L0 = LEDs [package=led10mm]
  R0L3 = LEDs [package=led10mm]
  R0L2 = LEDs [package=led10mm]
  R1L2 = LEDs [package=led10mm]
  R1L0 = LEDs [package=led10mm]
  R1L3 = LEDs [package=led10mm]
  R1L1 = LEDs [package=led10mm]
  R0L4 = LEDs [package=led10mm]
  R0L7 = LEDs [package=led10mm]
  R0L6 = LEDs [package=led10mm]
  R0L5 = LEDs [package=led10mm]
  R2L0 = LEDs [package=led10mm]
  R2L3 = LEDs [package=led10mm]
  R2L2 = LEDs [package=led10mm]
  R2L1 = LEDs [package=led10mm]
  R3L3 = LEDs [package=led10mm]
  R3L2 = LEDs [package=led10mm]
  R3L0 = LEDs [package=led10mm]
  R3L1 = LEDs [package=led10mm]
  R4L3 = LEDs [package=led10mm]
  R4L0 = LEDs [package=led10mm]
  R4L2 = LEDs [package=led10mm]
  R4L1 = LEDs [package=led10mm]
  R4L5 = LEDs [package=led10mm]
  R4L4 = LEDs [package=led10mm]
  R5L1 = LEDs [package=led10mm]
  R5L0 = LEDs [package=led10mm]
  R5L2 = LEDs [package=led10mm]
  R5L4 = LEDs [package=led10mm]
  R5L3 = LEDs [package=led10mm]
  R6L5 = LEDs [package=led10mm]
  R6L0 = LEDs [package=led10mm]
  R6L1 = LEDs [package=led10mm]
  R6L2 = LEDs [package=led10mm]
  R7L0 = LEDs [package=led10mm]
  R7L1 = LEDs [package=led10mm]
  R8L0 = LEDs [package=led10mm]
  R8L6 = LEDs [package=led10mm]
  R8L1 = LEDs [package=led10mm]
  R8L4 = LEDs [package=led10mm]
  R8L5 = LEDs [package=led10mm]
  R9L0 = LEDs [package=led10mm]
  R9L6 = LEDs [package=led10mm]
  R9L2 = LEDs [package=led10mm]
  R9L1 = LEDs [package=led10mm]
  R9L4 = LEDs [package=led10mm]
  R9L3 = LEDs [package=led10mm]
  R9L5 = LEDs [package=led10mm]
  R7L6 = LEDs [package=led10mm]
  R7L2 = LEDs [package=led10mm]
  R7L3 = LEDs [package=led10mm]
  R7L5 = LEDs [package=led10mm]
  R7L4 = LEDs [package=led10mm]
  R6L3 = LEDs [package=led10mm]
  R6L4 = LEDs [package=led10mm]
  R8L3 = LEDs [package=led10mm]
  R8L2 = LEDs [package=led10mm]
  SP1 = SPEAKER [package=pcb_mount_speaker]
  SP2 = SPEAKER [package=pcb_mount_speaker]
  S1 = Round Pushbutton
  Part1 = Arduino Mega 2560 (Rev3)
  KY-1 = Keyes Relay [package=THT]
  KY-2 = Keyes Relay [package=THT]
  VCC1 = Battery block 9V

nets:
  N1: R0L1.C, R0L0.C, R0L3.C, R0L2.C, R1L2.C, R1L0.C, R1L3.C, R1L1.C, R0L4.C, R0L7.C, R0L6.C, R0L5.C, R2L0.C, R2L3.C, R2L2.C, R2L1.C, R3L3.C, R3L2.C, R3L0.C, R3L1.C, R4L3.C, R4L0.C, R4L2.C, R4L1.C, R4L5.C, R4L4.C, R5L1.C, R5L0.C, R5L2.C, R5L4.C, R5L3.C, R6L5.C, R6L0.C, R6L1.C, R6L2.C, R7L0.C, R7L1.C, R8L0.C, R8L6.C, R8L1.C, R8L4.C, R8L5.C, R9L0.C, R9L6.C, R9L2.C, R9L1.C, R9L4.C, R9L3.C, R9L5.C, R7L6.C, R7L2.C, R7L3.C, R7L5.C, R7L4.C, R6L3.C, R6L4.C, R8L3.C, R8L2.C, SP1.+, SP2.+, Part1.GND, KY-1.ground, KY-1.NO, KY-2.NO
  N2: R0L1.A, Part1.D2_PWM
  N3: R0L0.A, Part1.D3_PWM
  N4: R0L3.A, Part1.D5_PWM
  N5: R0L2.A, Part1.D4_PWM
  N6: R1L2.A, Part1.D12_PWM
  N7: R1L0.A, Part1.D10_PWM
  N8: R1L3.A, Part1.D13_PWM
  N9: R1L1.A, Part1.D11_PWM
  N10: R0L4.A, Part1.D6_PWM
  N11: R0L7.A, Part1.D9_PWM
  N12: R0L6.A, Part1.D8_PWM
  N13: R0L5.A, Part1.D7_PWM
  N14: R2L0.A, Part1.D14/TX3
  N15: R2L3.A, Part1.D17_PWM/RX2
  N16: R2L2.A, Part1.D16_PWM/TX2
  N17: R2L1.A, Part1.D15/RX3
  N18: R3L3.A, Part1.D21/SCL, Part1.SCL
  N19: R3L2.A, Part1.D20/SDA, Part1.SDA
  N20: R3L0.A, Part1.D18/TX1
  N21: R3L1.A, Part1.D19/RX1
  N22: R4L3.A, Part1.D25
  N23: R4L0.A, Part1.D22
  N24: R4L2.A, Part1.D24
  N25: R4L1.A, Part1.D23
  N26: R4L5.A, Part1.D27
  N27: R4L4.A, Part1.D26
  N28: R5L1.A, Part1.D29
  N29: R5L0.A, Part1.D28
  N30: R5L2.A, Part1.D30
  N31: R5L4.A, Part1.D32
  N32: R5L3.A, Part1.D31
  N33: R6L5.A, Part1.D38
  N34: R6L0.A, Part1.D33
  N35: R6L1.A, Part1.D34
  N36: R6L2.A, Part1.D35
  N37: R7L0.A, Part1.D39
  N38: R7L1.A, Part1.D40
  N39: R8L0.A, Part1.A0
  N40: R8L6.A, Part1.A6
  N41: R8L1.A, Part1.A1
  N42: R8L4.A, Part1.A4
  N43: R8L5.A, Part1.A5
  N44: R9L0.A, Part1.A7
  N45: R9L6.A, Part1.A13
  N46: R9L2.A, Part1.A9
  N47: R9L1.A, Part1.A8
  N48: R9L4.A, Part1.A11
  N49: R9L3.A, Part1.A10
  N50: R9L5.A, Part1.A12
  N51: R7L6.A, Part1.D45
  N52: R7L2.A, Part1.D41
  N53: R7L3.A, Part1.D42
  N54: R7L5.A, Part1.D44
  N55: R7L4.A, Part1.D43
  N56: R6L3.A, Part1.D36
  N57: R6L4.A, Part1.D37
  N58: R8L3.A, Part1.A3
  N59: R8L2.A, Part1.A2
  N60: SP1.-, SP2.-, Part1.D49
  N61: S1.leg0, KY-1.C, KY-2.C, VCC1.-
  N62: S1.leg1, KY-2.signal, KY-2.ground
  N63: Part1.5V, KY-1.power
  N64: Part1.VIN, KY-2.power, VCC1.+
  N65: Part1.D48, KY-1.signal

custom parts:
  Keyes Relay: The Keyes 5V relay module is suitable for SCM development, home appliance control. It uses a 5V~12V TIL control signal which can control DC / AC signal.
